# Fritzing sketch esp8266_max485 (saved by Fritzing 0.9.4)
breadboards: 1

parts:
  U1 = NodeMCU V1.0
  RS485_module1 = RS485 Module (MAX3485)

nets:
  N1: U1.D1, RS485_module1.RE, RS485_module1.DE
  N2: U1.D2, RS485_module1.RO
  N3: U1.D3, RS485_module1.DI
  GND: U1.GND, RS485_module1.GND
  VIN: U1.Vin, RS485_module1.VCC

notes:
  Smart Heater

custom parts:
  NodeMCU V1.0: ESP8266 based NodeMCU
  RS485 Module (MAX3485): Commercially available RS485 to RS232 TTL Module
